# Fritzing sketch relay (saved by Fritzing 0.9.2b)
breadboards: 1

parts:
  元件1 = Arduino Uno (Rev3)
  U1 = G3VM-61E1 [package=g3vm-61e1]
  U2 = G3VM-61E1 [package=g3vm-61e1]
  LCD1 = I2c LCD
  S1 = Pushbutton [package=THT]
  S2 = Pushbutton [package=THT]

nets:
  N1: 元件1.A4/SDA, LCD1.SDA
  N2: 元件1.A5/SCL, LCD1.SCL
  N3: 元件1.D8, S1.leg1
  N4: 元件1.D2, U2.P$2
  N5: 元件1.D4, U1.P$2
  N6: 元件1.D7, S2.leg1
  5V: 元件1.5V, U1.P$1, U2.P$1, LCD1.VCC
  GND: 元件1.GND, U1.P$3, U2.P$3, LCD1.GND, S1.leg0, S2.leg0

custom parts:
  I2c LCD: A standard character display, usually with 2x16 characters. Comes in many colors.
